# Fritzing sketch Schematic (saved by Fritzing 0.9.3b)

parts:
  Part1 = Arduino Nano (Rev3.0) (ICSP)
  LCD1 = LCD screen
  R1 = Trimmer Potentiometer [maximum_resistance=10kΩ package=THT]
  R2 = Resistor [tolerance=±5% resistance=220 package="2010 [SMD]"]
  J1 = Piezo Speaker
  S1 = Pushbutton [package="[SMD]"]
  R3 = Resistor [tolerance=±5% resistance=10k package="2010 [SMD]"]
  BAT1 = BC9VPC [package=bc9vpc]

nets:
  GND: Part1.GND, LCD1.VSS, LCD1.R/W, LCD1.LED-, R1.leg1, J1.pin1, BAT1.V-
  N1: Part1.D2, LCD1.DB7
  N2: Part1.D3, LCD1.DB6
  N3: Part1.D4, LCD1.DB5
  N4: Part1.D5, LCD1.DB4
  N5: Part1.D10, J1.pin2
  N6: Part1.D11/MOSI, LCD1.E
  N7: Part1.D12/MISO, LCD1.RS
  N8: Part1.VIN, BAT1.V+
  5V: Part1.5V, LCD1.VDD, R1.leg2, R2.Pin_0, S1.Pin_3, S1.Pin_4, R3.Pin_1
  N9: Part1.A6, S1.Pin_1, S1.Pin_2
  N10: LCD1.V0, R1.wiper
  N11: LCD1.LED+, R2.Pin_1
